# Fritzing sketch Electronique (saved by Fritzing 0.9.2b)

parts:
  U4 = HIH-4030 [package=hih-4030]
  U5 = HIH-4030 [package=hih-4030]
  U6 = LM2596 voltage regulator [package=sot23-5]
  Battery_12V_12Ah = Battery 12V 12Ah
  Joystick_Gauche = Thumb Joystick
  Joystick_Droit = Thumb Joystick
  LED1 = LED - 5mm [color="Red (633nm)" package="5 mm [THT]"]
  U7 = SWITCH_SPDT [package=kps-1290]
  LED2 = LEDs [package=led-0603]
  LED3 = LEDs [package=led-0603]
  Arduino_Mega_2560_rev3 = Arduino Mega 2560 (Rev3)
  M1 = DC Motor
  M2 = DC Motor
  M3 = DC Motor
  M4 = DC Motor
  U8 = L298 [package=multiwatt15]
  U9 = L298 [package=multiwatt15]
  U10 = L298 [package=multiwatt15]

nets:
  N1: U4.OUT, Arduino_Mega_2560_rev3.D24
  N2: U5.GND, U8.CSA
  N3: U5.OUT, Arduino_Mega_2560_rev3.D25
  N4: U5.VCC, Arduino_Mega_2560_rev3.IOREF
  N5: U6.IN+, Battery_12V_12Ah.+
  N6: U6.IN-, U7.S
  VCC: U6.OUT+, Joystick_Gauche.VCC, Arduino_Mega_2560_rev3.VIN
  GND: U6.OUT-, Joystick_Gauche.GND, Joystick_Droit.GND, LED1.cathode, U8.GND
  N7: Battery_12V_12Ah.-, U7.P
  N8: Joystick_Gauche.SEL, Arduino_Mega_2560_rev3.A5
  N9: Joystick_Gauche.HORZ, Arduino_Mega_2560_rev3.A3
  N10: Joystick_Gauche.VERT, Arduino_Mega_2560_rev3.A4
  N11: Joystick_Droit.SEL, Arduino_Mega_2560_rev3.A2
  N12: Joystick_Droit.HORZ, Arduino_Mega_2560_rev3.A0
  N13: Joystick_Droit.VERT, Arduino_Mega_2560_rev3.A1
  N14: LED1.anode, Arduino_Mega_2560_rev3.A6
  N15: LED2.A, U10.OUT2
  N16: LED2.C, U10.OUT1
  N17: LED3.A, U10.OUT4
  N18: LED3.C, U10.OUT3
  N19: Arduino_Mega_2560_rev3.D13_PWM, U9.ENA
  N20: Arduino_Mega_2560_rev3.D12_PWM, U9.ENB
  N21: Arduino_Mega_2560_rev3.D11_PWM, U8.ENA
  N22: Arduino_Mega_2560_rev3.D10_PWM, U8.ENB
  N23: Arduino_Mega_2560_rev3.D26, U8.IN4
  N24: Arduino_Mega_2560_rev3.D27, U8.IN3
  N25: Arduino_Mega_2560_rev3.D28, U8.IN2
  N26: Arduino_Mega_2560_rev3.D29, U8.IN1
  N27: Arduino_Mega_2560_rev3.D30, U9.IN4
  N28: Arduino_Mega_2560_rev3.D31, U9.IN3
  N29: Arduino_Mega_2560_rev3.D32, U9.IN2
  N30: Arduino_Mega_2560_rev3.D33, U9.IN1
  N31: Arduino_Mega_2560_rev3.D34, U10.IN4
  N32: Arduino_Mega_2560_rev3.D35, U10.IN3
  N33: Arduino_Mega_2560_rev3.D36, U10.IN2
  N34: Arduino_Mega_2560_rev3.D37, U10.IN1
  GND_2: Arduino_Mega_2560_rev3.GND, U10.GND
  N35: M1.pin_1, U8.OUT3
  N36: M1.pin_2, U8.OUT4
  N37: M2.pin_1, U8.OUT1
  N38: M2.pin_2, U8.OUT2
  N39: M3.pin_1, U9.OUT3
  N40: M3.pin_2, U9.OUT4
  N41: M4.pin_1, U9.OUT1
  N42: M4.pin_2, U9.OUT2
  N43: U9.CSA, U10.CSA

custom parts:
  LM2596 voltage regulator: V_REG MIC5219 Standard 500mA LDO voltage regulator in SOT-23 layout. Micrel part MIC5219. BP (by-pass) pin is used to lower output noise with 470pF cap, may be left open.
